// Logisim project Projeto.circ as structural Verilog: 10 circuits, main circuit Maquina de Estados dos Registradores
module Maquina_de_Estados_dos_Registradores (
  output S1,
  output S0
);

  wire and_1_out, and_2_out, clock_1_out, clock_2_out, E___0_qn, or_1_out, xor_1_out, xor_2_out;

  Clock #(.highDuration(2), .lowDuration(4)) clock_1 (.out(clock_1_out));
  xor xor_1 (xor_1_out, clock_1_out, S1);
  and and_1 (and_1_out, S1, E___0_qn);
  and and_2 (and_2_out, S0, xor_1_out);
  Clock clock_2 (.out(clock_2_out));
  or or_1 (or_1_out, and_1_out, and_2_out);
  xor xor_2 (xor_2_out, clock_1_out, S0);
  D_Flip_Flop E___1 (.clk(clock_2_out), .D(or_1_out), .Q(S1));  // open: Qn, preset, en, reset
  D_Flip_Flop E___0 (.clk(clock_2_out), .D(xor_2_out), .Q(S0), .Qn(E___0_qn));  // open: preset, en, reset
endmodule

module Maquina_de_Estados_dos_Modos (
  input  in_1,
  output S1,
  output S0
);

  wire and_1_out, and_2_out, Clock_out, not_1_out, not_2_out, or_1_out, xor_1_out;

  xor xor_1 (xor_1_out, S1, S0);
  and and_1 (and_1_out, S1, not_1_out);
  not not_1 (not_1_out, in_1);
  and and_2 (and_2_out, in_1, xor_1_out);
  Clock Clock (.out(Clock_out));
  or or_1 (or_1_out, and_1_out, and_2_out);
  D_Flip_Flop E___1 (.clk(Clock_out), .D(or_1_out), .Q(S1));  // open: Qn, preset, en, reset
  D_Flip_Flop E___0 (.clk(Clock_out), .D(not_2_out), .Q(S0));  // open: Qn, preset, en, reset
  not not_2 (not_2_out, in_1);
endmodule

module Comparador (
  input  T1,
  input  S1,
  input  T0,
  input  S0,
  output S0_2
);

  wire xnor_1_out, xnor_2_out;

  xnor xnor_1 (xnor_1_out, T1, S1);
  xnor xnor_2 (xnor_2_out, T0, S0);
  and and_1 (S0_2, xnor_1_out, xnor_2_out);
endmodule

module Codificador (
  input  B3,
  input  B2,
  input  B1,
  input  B0,
  output S1,
  output S0
);

  or or_1 (S1, B3, B2);
  or or_2 (S0, B3, B1);
endmodule

module Decodificador (
  input  M,
  input  S1,
  input  S0,
  output S0_2,
  output S1_2,
  output S2,
  output S3,
  output S4,
  output S5,
  output S6,
  output S7
);

  wire not_1_out, not_2_out, not_3_out, not_4_out, not_5_out, not_6_out, not_7_out, not_8_out, not_9_out,
       not_10_out, not_11_out, not_12_out;

  not not_1 (not_1_out, M);
  not not_2 (not_2_out, S1);
  not not_3 (not_3_out, S0);
  not not_4 (not_4_out, M);
  not not_5 (not_5_out, S1);
  not not_6 (not_6_out, M);
  not not_7 (not_7_out, S0);
  not not_8 (not_8_out, M);
  not not_9 (not_9_out, S1);
  not not_10 (not_10_out, S0);
  not not_11 (not_11_out, S1);
  not not_12 (not_12_out, S0);
  and and_1 (S0_2, not_1_out, not_2_out, not_3_out);
  and and_2 (S1_2, not_4_out, not_5_out, S0);
  and and_3 (S2, not_6_out, S1, not_7_out);
  and and_4 (S3, not_8_out, S1, S0);
  and and_5 (S4, M, not_9_out, not_10_out);
  and and_6 (S5, M, not_11_out, S0);
  and and_7 (S6, M, S1, not_12_out);
  and and_8 (S7, M, S1, S0);
endmodule

module Hipocomp (
);

  wire and_1_out, and_2_out, and_3_out, B0_out, B1_out, B2_out, B3_out, Codificador_s0, Codificador_s1,
       comparador_1_s0_2, comparador_2_s0_2, comparador_3_s0_2, Comparadores_s0_2, Decodificador_s0_2,
       Decodificador_s1_2, Decodificador_s2, Decodificador_s3, Decodificador_s4, Decodificador_s5,
       Decodificador_s6, Decodificador_s7, M__E__Modos_s1, M__E__Registradores_s0, M__E__Registradores_s1,
       or_1_out, or_2_out, or_3_out, R0_s0, R0_s1, R1_s0, R1_s1, R2_s0, R2_s1, R3_s0, R3_s1, R4_s0, R4_s1,
       R5_s0, R5_s1, R6_s0, R6_s1, R7_s0, R7_s1, Registrador_s0, Registrador_s1, Registrador_s2,
       Registrador_s3;

  Button B3 (.out(B3_out));
  Button B2 (.out(B2_out));
  Button B1 (.out(B1_out));
  Button B0 (.out(B0_out));
  and and_1 (and_1_out, Decodificador_s3, or_1_out);
  or or_1 (or_1_out, B3_out, B2_out, B1_out, B0_out);
  Maquina_de_Estados_dos_Modos M__E__Modos (.in_1(or_2_out), .S1(M__E__Modos_s1));  // open: S0
  or or_2 (or_2_out, and_3_out, and_1_out);
  Prototipo M__E__Registradores (.in_1(or_1_out), .S1(M__E__Registradores_s1), .S0(M__E__Registradores_s0));
  Codificador Codificador (
    .B3(B3_out), .B2(B2_out), .B1(B1_out), .B0(B0_out), .S1(Codificador_s1), .S0(Codificador_s0));
  Decodificador Decodificador (
    .M(M__E__Modos_s1), .S1(M__E__Registradores_s1), .S0(M__E__Registradores_s0), .S0_2(Decodificador_s0_2),
    .S1_2(Decodificador_s1_2), .S2(Decodificador_s2), .S3(Decodificador_s3), .S4(Decodificador_s4),
    .S5(Decodificador_s5), .S6(Decodificador_s6), .S7(Decodificador_s7));
  Registrador_N R6 (
    .A1(Codificador_s1), .A0(Codificador_s0), .Enable(Decodificador_s6), .Reset(and_2_out), .S1(R6_s1),
    .S0(R6_s0));
  Registrador_S R7 (
    .A0(Codificador_s0), .A1(Codificador_s1), .Enable(Decodificador_s7), .Reset(and_2_out), .S0(R7_s0),
    .S1(R7_s1));
  Registrador_N R2 (
    .A1(Codificador_s1), .A0(Codificador_s0), .Enable(Decodificador_s2), .Reset(and_2_out), .S1(R2_s1),
    .S0(R2_s0));
  Registrador_N R4 (
    .A1(Codificador_s1), .A0(Codificador_s0), .Enable(Decodificador_s4), .Reset(and_2_out), .S1(R4_s1),
    .S0(R4_s0));
  Registrador_S R5 (
    .A0(Codificador_s0), .A1(Codificador_s1), .Enable(Decodificador_s5), .Reset(and_2_out), .S0(R5_s0),
    .S1(R5_s1));
  Registrador_N R0 (
    .A1(Codificador_s1), .A0(Codificador_s0), .Enable(Decodificador_s0_2), .Reset(and_2_out), .S1(R0_s1),
    .S0(R0_s0));
  Registrador_S R3 (
    .A0(Codificador_s0), .A1(Codificador_s1), .Enable(Decodificador_s3), .Reset(and_2_out), .S0(R3_s0),
    .S1(R3_s1));
  Registrador_S R1 (
    .A0(Codificador_s0), .A1(Codificador_s1), .Enable(Decodificador_s1_2), .Reset(and_2_out), .S0(R1_s0),
    .S1(R1_s1));
  or or_3 (or_3_out, Decodificador_s3, Decodificador_s4);
  Comparador Comparadores (.T1(R6_s1), .S1(R2_s1), .T0(R6_s0), .S0(R2_s0), .S0_2(Comparadores_s0_2));
  Comparador comparador_1 (.T1(R4_s1), .S1(R0_s1), .T0(R4_s0), .S0(R0_s0), .S0_2(comparador_1_s0_2));
  Comparador comparador_2 (.T1(R5_s1), .S1(R1_s1), .T0(R5_s0), .S0(R1_s0), .S0_2(comparador_2_s0_2));
  Comparador comparador_3 (.T1(R7_s1), .S1(R3_s1), .T0(R7_s0), .S0(R3_s0), .S0_2(comparador_3_s0_2));
  and and_2 (and_2_out, Decodificador_s0_2, Registrador_s0);
  LED led_1 (.in(Registrador_s2));
  LED led_2 (.in(Registrador_s3));
  Registrador_Final Registrador (
    .A3(comparador_1_s0_2), .A2(comparador_2_s0_2), .A1(Comparadores_s0_2), .A0(comparador_3_s0_2),
    .ENABLE(or_3_out), .RESET(and_2_out), .S3(Registrador_s3), .S2(Registrador_s2), .S1(Registrador_s1),
    .S0(Registrador_s0));
  LED led_3 (.in(Registrador_s1));
  LED led_4 (.in(Registrador_s0));
  and and_3 (and_3_out, Registrador_s3, Registrador_s2, Registrador_s1, Registrador_s0);
  LED led_5 (.in(and_3_out));
endmodule

module Registrador_S (
  input  A0,
  input  A1,
  input  Enable,
  input  Reset,
  output S0,
  output S1
);

  wire clock_1_out;

  Clock clock_1 (.out(clock_1_out));
  D_Flip_Flop d_ff_1 (.clk(clock_1_out), .D(A0), .Q(S0), .en(Enable), .reset(Reset));  // open: Qn, preset
  D_Flip_Flop d_ff_2 (.clk(clock_1_out), .D(A1), .Q(S1), .en(Enable), .reset(Reset));  // open: Qn, preset
endmodule

module Registrador_N (
  input  Enable,
  input  Reset,
  input  A1,
  input  A0,
  output S1,
  output S0
);

  wire clock_1_out;

  Clock clock_1 (.out(clock_1_out));
  D_Flip_Flop d_ff_1 (.clk(clock_1_out), .D(A1), .Q(S1), .en(Enable), .reset(Reset));  // open: Qn, preset
  D_Flip_Flop d_ff_2 (.clk(clock_1_out), .D(A0), .Q(S0), .en(Enable), .reset(Reset));  // open: Qn, preset
endmodule

module Registrador_Final (
  input  A3,
  input  A2,
  input  A1,
  input  A0,
  input  ENABLE,
  input  RESET,
  output S3,
  output S2,
  output S1,
  output S0
);

  wire CLOCK_out;

  Clock CLOCK (.out(CLOCK_out));
  D_Flip_Flop d_ff_1 (.clk(CLOCK_out), .D(A3), .Q(S3), .en(ENABLE), .reset(RESET));  // open: Qn, preset
  D_Flip_Flop d_ff_2 (.clk(CLOCK_out), .D(A2), .Q(S2), .en(ENABLE), .reset(RESET));  // open: Qn, preset
  D_Flip_Flop d_ff_3 (.clk(CLOCK_out), .D(A1), .Q(S1), .en(ENABLE), .reset(RESET));  // open: Qn, preset
  D_Flip_Flop d_ff_4 (.clk(CLOCK_out), .D(A0), .Q(S0), .en(ENABLE), .reset(RESET));  // open: Qn, preset
endmodule

module Prototipo (
  input  in_1,
  output S1,
  output S0
);

  wire and_1_out, and_2_out, clock_1_out, E___0_qn, or_1_out, xor_1_out, xor_2_out;

  xor xor_1 (xor_1_out, in_1, S1);
  and and_1 (and_1_out, S1, E___0_qn);
  and and_2 (and_2_out, S0, xor_1_out);
  Clock clock_1 (.out(clock_1_out));
  or or_1 (or_1_out, and_1_out, and_2_out);
  xor xor_2 (xor_2_out, in_1, S0);
  D_Flip_Flop E___1 (.clk(clock_1_out), .D(or_1_out), .Q(S1));  // open: Qn, preset, en, reset
  D_Flip_Flop E___0 (.clk(clock_1_out), .D(xor_2_out), .Q(S0), .Qn(E___0_qn));  // open: preset, en, reset
endmodule
